# Fritzing sketch Space Costume Schematic (saved by Fritzing 0.8.3b)

parts:
  FLORA1 = Adafruit_Flora
  LED1 = Adafruit_FLORA_RGB_Smart_Pixel
  LED2 = Adafruit_FLORA_RGB_Smart_Pixel
  LED3 = Adafruit_FLORA_RGB_Smart_Pixel
  LED4 = Adafruit_FLORA_RGB_Smart_Pixel
  LED5 = Adafruit_FLORA_RGB_Smart_Pixel
  LED6 = Adafruit_FLORA_RGB_Smart_Pixel
  LED7 = Adafruit_FLORA_RGB_Smart_Pixel
  LED8 = Adafruit_FLORA_RGB_Smart_Pixel
  LED9 = Adafruit_FLORA_RGB_Smart_Pixel
  LED10 = Adafruit_FLORA_RGB_Smart_Pixel
  LED11 = Adafruit_FLORA_RGB_Smart_Pixel
  LED12 = Adafruit_FLORA_RGB_Smart_Pixel

nets:
  N1: FLORA1.connector8, LED1.connector1, LED2.connector1, LED3.connector1, LED4.connector1, LED5.connector1, LED6.connector1, LED7.connector1, LED8.connector1, LED9.connector1, LED10.connector1, LED11.connector1, LED12.connector1
  N2: FLORA1.connector10, LED1.connector2
  N3: FLORA1.connector11, LED1.connector3, LED2.connector3, LED3.connector3, LED4.connector3, LED5.connector3, LED6.connector3, LED7.connector3, LED8.connector3, LED9.connector3, LED10.connector3, LED11.connector3, LED12.connector3
  N4: LED1.connector4, LED2.connector2
  N5: LED2.connector4, LED3.connector2
  N6: LED3.connector4, LED4.connector2
  N7: LED4.connector4, LED5.connector2
  N8: LED5.connector4, LED6.connector2
  N9: LED6.connector4, LED10.connector2
  N10: LED7.connector2, LED12.connector4
  N11: LED7.connector4, LED8.connector2
  N12: LED8.connector4, LED9.connector2
  N13: LED10.connector4, LED11.connector2
  N14: LED11.connector4, LED12.connector2
